# Fritzing sketch Untitled Sketch 2 (saved by Fritzing 0.8.7b)
breadboards: 1

parts:
  Parte1 = Arduino Mega 2560 (Rev3)
  LED1 = LED - 5mm [color="Red (633nm)" package="5 mm [THT]"]
  LED2 = LED - 5mm [color="Green (565nm)" package="5 mm [THT]"]
  RHT1 = Humidity and Temperature Sensor RHT03
  R1 = Resistor [tolerance=±5% resistance=10k package=THT]

nets:
  N1: Parte1.GND, LED1.cathode, LED2.cathode, RHT1.GND_2
  N2: Parte1.D10_PWM, LED1.anode
  N3: Parte1.D8_PWM, LED2.anode
  5V: Parte1.5V, RHT1.Vcc, R1.Pin_1
  N4: Parte1.D6_PWM, RHT1.Data-signal, R1.Pin_0
